# Fritzing sketch Self_balance (saved by Fritzing 0.9.1b)
breadboards: 1

parts:
  IC1 = L293D [package=THT]
  GY2 = MPU-6050 Board GY-521 [form="♀ (female)" package=THT]
  Part2 = Bluetooth HC-05 Macho
  IC2 = Voltage Regulator [package=to-220-alt]
  M1 = DC Motor
  M2 = DC Motor
  Power_plug1 = Power plug
  VCC1 = Battery block 9V
  Part3 = Arduino Uno (Rev3)

nets:
  N1: IC1.Enable_1, Part3.D9_PWM
  N2: IC1.In_1, Part3.D5_PWM
  N3: IC1.Out_1_(_Controlled_by_Enable_1_), M2.pin_1
  GND: IC1.0V, GY2.pin2, Part2.GND, IC2.IN, Power_plug1.GND, VCC1.-, Part3.GND
  N4: IC1.Out_2_(_Controlled_by_Enable_1_), M2.pin_2
  N5: IC1.In_2, Part3.D8
  N6: IC1.+Vmotor, IC2.GND, VCC1.+
  N7: IC1.Enable_2, Part3.D10_PWM/SS
  N8: IC1.In_3, Part3.D12/MISO
  N9: IC1.Out_3_(_Controlled_by_Enable_2_), M1.pin_2
  N10: IC1.Out_4_(_Controlled_by_Enable_2_), M1.pin_1
  N11: IC1.In_4, Part3.D6_PWM
  VCC: IC1.+V, GY2.pin1, Part2.VCC, Part3.3V3, Part3.5V
  N12: GY2.pin3, Part3.A5/SCL
  N13: GY2.pin4, Part3.A4/SDA
  N14: GY2.pin8, Part3.D2
  N15: Part2.TXD, Part3.D11_PWM/MOSI
  N16: IC2.OUT, Power_plug1.VCC

notes:
  3.3V line
  5V line
  12V line
  MPU-6050
  L293D
  HC-05 Bluetooh Module
  Battery
  500rpm Motors
  IC-7805 Vlotage Regulator

custom parts:
  MPU-6050 Board GY-521: Acelerometro y Giroscopio MPU-6050 Board GY-521
